# Fritzing sketch rocket-clock (saved by Fritzing 0.9.3b)

parts:
  ESP8266 = NodeMCU V3.0
  R1 = Resistor [tolerance=±5% resistance=220 package="0603 [SMD]"]
  R2 = Resistor [tolerance=±5% resistance=220 package="0603 [SMD]"]
  Day_LED_(Red) = LED - 5mm [color="Red (633nm)" package="5 mm [THT]"]
  Night_LED_(Blue) = LED - 5mm [color="Blue (430nm)" package="5 mm [THT]"]

nets:
  N1: ESP8266.GND, Day_LED_(Red).cathode, Night_LED_(Blue).cathode
  N2: ESP8266.D5, R1.Pin_0
  N3: ESP8266.D6, R2.Pin_0
  N4: R1.Pin_1, Night_LED_(Blue).anode
  N5: R2.Pin_1, Day_LED_(Red).anode

custom parts:
  NodeMCU V3.0: ESP8266 based NodeMCU
